# Fritzing sketch Schaltplan (saved by Fritzing 0.9.3b)

parts:
  U1 = 2.4" TFT LCD screen, SPI, Touch-enabled
  WeMos_D1_Mini1 = WeMos D1 Mini
  S1 = Momentary Switch [package=tactile-pth]
  R1 = Resistor [tolerance=±5% resistance=1k package="0805 [SMD]"]

nets:
  N1: U1.T_IRQ, WeMos_D1_Mini1.D1
  N2: U1.T_DO, U1.SDO, WeMos_D1_Mini1.D6
  N3: U1.T_DIN, U1.SDA, WeMos_D1_Mini1.D7
  N4: U1.T_CS, WeMos_D1_Mini1.D2
  N5: U1.T_CLK, U1.SCL, WeMos_D1_Mini1.D5
  VCC: U1.LED, U1.RESET, U1.VCC, WeMos_D1_Mini1.3V3, R1.Pin_1
  N6: U1.DC, WeMos_D1_Mini1.D4
  N7: U1.CS, WeMos_D1_Mini1.D8
  N8: U1.GND, WeMos_D1_Mini1.G, S1.3, S1.4
  N9: S1.1, S1.2, R1.Pin_0

custom parts:
  2.4" TFT LCD screen, SPI, Touch-enabled: 2.4", ILI9341-based TFT LCD screen with touch-sensing using the XPT2046 controller, SPI-compatible. There is also an SD-card version that is non-touch enabled but uses exactly the same board and pinout. This part is for both, though it should be noted that the SD reader and the touch screen are mutually incompatible
